// Digital circuit adder.dig as structural Verilog
module adder (
  input  [7:0] x,
  input  [7:0] y,
  input  op,
  output [8:0] z
);

  wire fac_1_p2, fac_1_p4, fac_2_p3, fac_3_p3, fac_3_p5, fac_4_p3, fac_4_p5, fac_5_p3, fac_5_p5, fac_6_p3,
       fac_6_p5, fac_7_p3, fac_7_p5, fac_8_p3, fac_8_p5, fac_9_p5;

  // fac fac_1: pin names not known; wires that end beside it: z[8], fac_1_p2, x[7], fac_1_p4
  // fac fac_2: pin names not known; wires that end beside it: fac_1_p2, z[7], fac_2_p3, x[7], fac_1_p4
  xor xor_1 (fac_1_p4, y[7], op);
  // fac fac_3: pin names not known; wires that end beside it: fac_2_p3, z[6], fac_3_p3, x[6], fac_3_p5
  xor xor_2 (fac_3_p5, y[6], op);
  // fac fac_4: pin names not known; wires that end beside it: fac_3_p3, z[5], fac_4_p3, x[5], fac_4_p5
  xor xor_3 (fac_4_p5, y[5], op);
  // fac fac_5: pin names not known; wires that end beside it: fac_4_p3, z[4], fac_5_p3, x[4], fac_5_p5
  xor xor_4 (fac_5_p5, y[4], op);
  // fac fac_6: pin names not known; wires that end beside it: fac_5_p3, z[3], fac_6_p3, x[3], fac_6_p5
  xor xor_5 (fac_6_p5, y[3], op);
  // fac fac_7: pin names not known; wires that end beside it: fac_6_p3, z[2], fac_7_p3, x[2], fac_7_p5
  xor xor_6 (fac_7_p5, y[2], op);
  // fac fac_8: pin names not known; wires that end beside it: fac_7_p3, z[1], fac_8_p3, x[1], fac_8_p5
  xor xor_7 (fac_8_p5, y[1], op);
  // fac fac_9: pin names not known; wires that end beside it: fac_8_p3, z[0], op, x[0], fac_9_p5
  xor xor_8 (fac_9_p5, y[0], op);

  // Notes on the sheet:
  //   0 = adder
  //   1 = subtractor
endmodule
