// Digital circuit cnt.dig as structural Verilog
module cnt (
  input  rst,
  input  clk,
  input  incr,
  output [2:0] out
);

  wire and_1_out, and_2_out, and_3_out, and_4_out, and_5_out, not_1_out, xor_1_out, xor_2_out, xor_3_out;

  not not_1 (not_1_out, rst);
  and and_1 (and_1_out, xor_1_out, not_1_out);
  d_ff b0 (.d(and_1_out), .clk(clk), .q(out[0]));  // open: nq
  xor xor_1 (xor_1_out, out[0], incr);
  and and_2 (and_2_out, out[0], incr);
  xor xor_2 (xor_2_out, out[1], and_2_out);
  and and_3 (and_3_out, xor_2_out, not_1_out);
  d_ff b1 (.d(and_3_out), .clk(clk), .q(out[1]));  // open: nq
  and and_4 (and_4_out, out[1], out[0], incr);
  xor xor_3 (xor_3_out, out[2], and_4_out);
  and and_5 (and_5_out, xor_3_out, not_1_out);
  d_ff b2 (.d(and_5_out), .clk(clk), .q(out[2]));  // open: nq
endmodule
