// Digital circuit d_ff.dig as structural Verilog
module d_ff (
  input  d,
  input  clk,
  output q,
  output nq
);

  wire master_q, not_1_out, not_2_out;

  not not_1 (not_1_out, clk);
  d_latch master (.d(d), .e(not_1_out), .q(master_q));  // open: nq
  not not_2 (not_2_out, not_1_out);
  d_latch slave (.d(master_q), .e(not_2_out), .q(q), .nq(nq));
endmodule
