// Digital circuit d_latch.dig as structural Verilog
module d_latch (
  input  d,
  input  e,
  output q,
  output nq
);

  wire and_1_out, and_2_out, not_1_out;

  not not_1 (not_1_out, d);
  and and_1 (and_1_out, not_1_out, e);
  and and_2 (and_2_out, e, d);
  nor nor_1 (q, and_1_out, nq);
  nor nor_2 (nq, q, and_2_out);
endmodule
