// Digital circuit reg_1.dig as structural Verilog
module reg_1 (
  input  in,
  input  load,
  input  clk,
  input  rst,
  output out
);

  wire and_1_out, and_2_out, and_3_out, not_1_out, not_2_out, or_1_out;

  not not_1 (not_1_out, rst);
  and and_1 (and_1_out, or_1_out, not_1_out);
  d_ff d_ff_1 (.d(and_1_out), .clk(clk), .q(out));  // open: nq
  or or_1 (or_1_out, and_3_out, and_2_out);
  and and_2 (and_2_out, in, load);
  and and_3 (and_3_out, out, not_2_out);
  not not_2 (not_2_out, load);
endmodule
