// Digital circuit reg_4.dig as structural Verilog
module reg_4 (
  input  clk,
  input  rst,
  input  [7:0] in,
  input  load,
  output [7:0] out
);

  wire and_1_out, and_2_out, and_3_out, and_4_out, not_1_out;
  wire [7:0] multiplexer_1_out;

  and and_1 (and_1_out, multiplexer_1_out[3], not_1_out);
  d_ff d_ff_1 (.d(and_1_out), .clk(clk), .q(out[3]));  // open: nq
  and and_2 (and_2_out, multiplexer_1_out[2], not_1_out);
  d_ff d_ff_2 (.d(and_2_out), .clk(clk), .q(out[2]));  // open: nq
  and and_3 (and_3_out, multiplexer_1_out[1], not_1_out);
  d_ff d_ff_3 (.d(and_3_out), .clk(clk), .q(out[1]));  // open: nq
  and and_4 (and_4_out, multiplexer_1_out[0], not_1_out);
  d_ff d_ff_4 (.d(and_4_out), .clk(clk), .q(out[0]));  // open: nq
  not not_1 (not_1_out, rst);
  Multiplexer #(.Bits(8)) multiplexer_1 (.sel(load), .in_0(out), .in_1(in), .out(multiplexer_1_out));
  // Pins of 4 and 8 bits meet at in
  // Pins of 4 and 8 bits meet at out
  // Pins of 4 and 8 bits meet at multiplexer_1_out
endmodule
