// Digital circuit shift_reg.dig as structural Verilog
module shift_reg (
  input  clk,
  input  rst,
  input  [7:0] in,
  input  b7,
  input  b0,
  input  [1:0] sel,
  input  load,
  output [7:0] out
);

  wire and_1_out, and_2_out, and_3_out, and_4_out, and_5_out, and_6_out, and_7_out, and_8_out, not_1_out;
  wire [0:0] d_ff_8_q;
  wire [6:0] d_ff_1_q;
  wire [7:0] multiplexer_2_out;

  and and_1 (and_1_out, multiplexer_2_out[7], not_1_out);
  d_ff d_ff_1 (.d(and_1_out), .clk(clk), .q(d_ff_1_q[6]));  // open: nq
  and and_2 (and_2_out, multiplexer_2_out[6], not_1_out);
  d_ff d_ff_2 (.d(and_2_out), .clk(clk), .q(d_ff_1_q[5]));  // open: nq
  and and_3 (and_3_out, multiplexer_2_out[5], not_1_out);
  d_ff d_ff_3 (.d(and_3_out), .clk(clk), .q(d_ff_1_q[4]));  // open: nq
  and and_4 (and_4_out, multiplexer_2_out[4], not_1_out);
  d_ff d_ff_4 (.d(and_4_out), .clk(clk), .q(d_ff_1_q[3]));  // open: nq
  and and_5 (and_5_out, multiplexer_2_out[3], not_1_out);
  d_ff d_ff_5 (.d(and_5_out), .clk(clk), .q(d_ff_1_q[2]));  // open: nq
  and and_6 (and_6_out, multiplexer_2_out[2], not_1_out);
  d_ff d_ff_6 (.d(and_6_out), .clk(clk), .q(d_ff_1_q[1]));  // open: nq
  and and_7 (and_7_out, multiplexer_2_out[1], not_1_out);
  d_ff d_ff_7 (.d(and_7_out), .clk(clk), .q(d_ff_1_q[0]));  // open: nq
  and and_8 (and_8_out, multiplexer_2_out[0], not_1_out);
  d_ff d_ff_8 (.d(and_8_out), .clk(clk), .q(d_ff_8_q[0]));  // open: nq
  not not_1 (not_1_out, rst);
  Multiplexer #(.Selector_Bits(2), .Bits(8)) multiplexer_1 (
    .sel(sel), .in_0({d_ff_1_q, d_ff_8_q[0]}), .in_1({b7, d_ff_1_q}),
    .in_2({d_ff_1_q[5:0], d_ff_8_q[0], b0}), .in_3({d_ff_1_q, d_ff_8_q[0]}), .out(out));
  Multiplexer #(.Bits(8)) multiplexer_2 (.sel(load), .in_0(out), .in_1(in), .out(multiplexer_2_out));

  // Notes on the sheet:
  //   when shifting right
  //   00/11 = normal
  //   01 = rshift
  //   10 = lshift
  //   when shifting left
endmodule
