// Digital circuit shift_reg_16.dig as structural Verilog
module shift_reg_16 (
  input  clk,
  input  rst,
  input  [15:0] in,
  input  [1:0] load,
  input  bit_in,
  input  [1:0] sel,
  output [15:0] out,
  output bit_out
);

  wire A_bit_out, multiplexer_1_out, multiplexer_2_out, not_1_out, Q_bit_out;

  not not_1 (not_1_out, sel[0]);
  Multiplexer multiplexer_1 (.sel(not_1_out), .in_0(bit_in), .in_1(Q_bit_out), .out(multiplexer_1_out));
  shift_reg_8 A (
    .clk(clk), .rst(rst), .in(in[15:8]), .load(load[1]), .sel(sel), .bit_in(multiplexer_1_out),
    .out(out[15:8]), .bit_out(A_bit_out));
  Multiplexer multiplexer_2 (.sel(not_1_out), .in_0(A_bit_out), .in_1(bit_in), .out(multiplexer_2_out));
  shift_reg_8 Q (
    .clk(clk), .rst(rst), .in(in[7:0]), .load(load[0]), .sel(sel), .bit_in(multiplexer_2_out),
    .out(out[7:0]), .bit_out(Q_bit_out));
  Multiplexer multiplexer_3 (.sel(not_1_out), .in_0(Q_bit_out), .in_1(A_bit_out), .out(bit_out));

  // Notes on the sheet:
  //   sel[1] -> 
  //   0 = disabled
  //                   1 = enabled
  //   sel[0] ->
  //   0 = Lshift
  //                   1 = Rshift
endmodule
